# Fritzing sketch schematics (saved by Fritzing 0.9.3b)
breadboards: 2

parts:
  S1 = Pushbutton [package="[SMD]"]
  S2 = Pushbutton [package="[SMD]"]
  S3 = Pushbutton [package="[SMD]"]
  S4 = Pushbutton [package="[SMD]"]
  S5 = Pushbutton [package="[SMD]"]
  S6 = Pushbutton [package="[SMD]"]
  Part1 = Arduino Pro Mini v13
  Part3 = RFID-RC522-v3
  R1 = Resistor [tolerance=±5% resistance=220 package=THT]
  R2 = Resistor [tolerance=±5% resistance=220 package=THT]
  R3 = Resistor [tolerance=±5% resistance=220 package=THT]
  R4 = Resistor [tolerance=±5% resistance=220 package=THT]
  R5 = Resistor [tolerance=±5% resistance=220 package=THT]
  R6 = Resistor [tolerance=±5% resistance=1k package=THT]

nets:
  N1: S1.Pin_1, S1.Pin_2, S2.Pin_1, S2.Pin_2, S3.Pin_1, S3.Pin_2, S4.Pin_1, S4.Pin_2, S5.Pin_1, S5.Pin_2, S6.Pin_1, S6.Pin_2
  N2: S1.Pin_3, S1.Pin_4, R1.Pin_1
  N3: S2.Pin_3, S2.Pin_4, R2.Pin_1
  N4: S3.Pin_3, S3.Pin_4, R3.Pin_1
  N5: S4.Pin_3, S4.Pin_4, R4.Pin_1
  N6: S5.Pin_3, S5.Pin_4, R5.Pin_1
  N7: S6.Pin_3, S6.Pin_4, R6.Pin_1
  N8: Part1.RAW, Part3.3.3V
  GND: Part1.GND, Part3.GND
  N9: Part1.D13/SCK, Part3.SCK
  N10: Part1.D12/MISO, Part3.MISO
  N11: Part1.D11_PWM/MOSI, Part3.MOSI
  N12: Part1.D10_PWM/SS, Part3.SDA
  N13: Part1.D9_PWM, Part3.RST
  N14: R1.Pin_0, R2.Pin_0, R3.Pin_0, R4.Pin_0, R5.Pin_0, R6.Pin_0

custom parts:
  RFID-RC522-v3: A simple China made RFID-RC522 Reader (6x4 cm); do check the pin labels, as this is a MFRC522 based clone.
